// Digital circuit Mux16.dig as structural Verilog
module Mux16 (
  input  a_0,
  input  b_0,
  input  sel,
  input  a_1,
  input  b_1,
  input  a_2,
  input  b_2,
  input  a_3,
  input  b_3,
  input  a_4,
  input  b_4,
  input  a_5,
  input  b_5,
  input  a_6,
  input  b_6,
  input  a_7,
  input  b_7,
  input  a_8,
  input  b_8,
  input  a_9,
  input  b_9,
  input  a_10,
  input  b_10,
  input  a_11,
  input  b_11,
  input  a_12,
  input  b_12,
  input  a_13,
  input  b_13,
  input  a_14,
  input  b_14,
  input  a_15,
  input  b_15,
  output out_3,
  output out_7,
  output out_10,
  output out_13,
  output out_16,
  output out_19,
  output out_22,
  output out_25,
  output out_28,
  output out_31,
  output out_34,
  output out_37,
  output out_40,
  output out_43,
  output out_46,
  output out_49
);

  Multiplexer multiplexer_1 (.sel(sel), .in_0(a_0), .in_1(b_0), .out(out_3));
  Multiplexer multiplexer_2 (.sel(sel), .in_0(a_1), .in_1(b_1), .out(out_7));
  Multiplexer multiplexer_3 (.sel(sel), .in_0(a_2), .in_1(b_2), .out(out_10));
  Multiplexer multiplexer_4 (.sel(sel), .in_0(a_3), .in_1(b_3), .out(out_13));
  Multiplexer multiplexer_5 (.sel(sel), .in_0(a_4), .in_1(b_4), .out(out_16));
  Multiplexer multiplexer_6 (.sel(sel), .in_0(a_5), .in_1(b_5), .out(out_19));
  Multiplexer multiplexer_7 (.sel(sel), .in_0(a_6), .in_1(b_6), .out(out_22));
  Multiplexer multiplexer_8 (.sel(sel), .in_0(a_7), .in_1(b_7), .out(out_25));
  Multiplexer multiplexer_9 (.sel(sel), .in_0(a_8), .in_1(b_8), .out(out_28));
  Multiplexer multiplexer_10 (.sel(sel), .in_0(a_9), .in_1(b_9), .out(out_31));
  Multiplexer multiplexer_11 (.sel(sel), .in_0(a_10), .in_1(b_10), .out(out_34));
  Multiplexer multiplexer_12 (.sel(sel), .in_0(a_11), .in_1(b_11), .out(out_37));
  Multiplexer multiplexer_13 (.sel(sel), .in_0(a_12), .in_1(b_12), .out(out_40));
  Multiplexer multiplexer_14 (.sel(sel), .in_0(a_13), .in_1(b_13), .out(out_43));
  Multiplexer multiplexer_15 (.sel(sel), .in_0(a_14), .in_1(b_14), .out(out_46));
  Multiplexer multiplexer_16 (.sel(sel), .in_0(a_15), .in_1(b_15), .out(out_49));
endmodule
